# Fritzing sketch ros-robot (saved by Fritzing 0.9.3b)
breadboards: 1

parts:
  IC1 = H-Bridge [package=THT]
  BeagleBone1 = BeagleBone Black
  M1 = DC Motor
  M2 = DC Motor
  R1 = Resistor [tolerance=±5% resistance=1k package=THT]
  R2 = Resistor [tolerance=±5% resistance=1k package=THT]
  R3 = Resistor [tolerance=±5% resistance=1k package=THT]
  R4 = Resistor [tolerance=±5% resistance=1k package=THT]

nets:
  N1: IC1.1_2EN, IC1.3_4EN, BeagleBone1.no_name_yet#5
  N2: IC1.1A, BeagleBone1.no_name_yet#11, BeagleBone1.no_name_yet#12, R1.Pin_0
  N3: IC1.1Y, M1.pin_2
  GND1: IC1.GND1, IC1.GND2, IC1.GND3, IC1.GND4, BeagleBone1.no_name_yet#2, R1.Pin_1, R2.Pin_1, R3.Pin_1, R4.Pin_1
  N4: IC1.2Y, M1.pin_1
  N5: IC1.2A, BeagleBone1.no_name_yet#23, R2.Pin_0
  N6: IC1.VCC2, IC1.VCC1, BeagleBone1.no_name_yet#7
  N7: IC1.3A, BeagleBone1.no_name_yet#27, R3.Pin_0
  N8: IC1.3Y, M2.pin_2
  N9: IC1.4Y, M2.pin_1
  N10: IC1.4A, BeagleBone1.no_name_yet#25, R4.Pin_0

custom parts:
  BeagleBone Black: BeagleBone Black rev. A5B
